# Fritzing sketch MAX31855K_Breakout (saved by Fritzing 0.9.2b)

parts:
  Part1 = FTDI Basic Programmer
  Part2 = Arduino Pro Mini v13

nets:
  N1: Part1.DTR, Part2.DTR
  N2: Part1.RXI, Part2.D0/TX
  N3: Part1.TXO, Part2.D1/RX
  N4: Part1.POWER, Part2.VCC
  GND: Part1.CTS, Part1.GND, Part2.GND
